// Logisim project 6 bit CPU-DESIGN.circ as structural Verilog: 22 circuits, main circuit 6 bit XOR Gate
module _6_bit_XOR_Gate (
  input  [5:0] A,
  input  [5:0] B,
  output [5:0] O
);

  xor xor_1 (O[0], A[5], B[0]);
  xor xor_2 (O[1], A[4], B[1]);
  xor xor_3 (O[2], A[3], B[2]);
  xor xor_4 (O[3], A[2], B[3]);
  xor xor_5 (O[4], A[1], B[4]);
  xor xor_6 (O[5], A[0], B[5]);

  // Other names for the same wires on the sheet: B5 = B[0]; B4 = B[1]; B3 = B[2]; B2 = B[3]; B1 = B[4]; B0 = B[5];
  //   O5 = O[0]; O4 = O[1]; O3 = O[2]; O2 = O[3]; O1 = O[4]; O0 = O[5]
endmodule

module _6_bit_XOR_Gate_Testing (
  input  [5:0] in_1,
  input  [5:0] in_2,
  output [5:0] out_3
);

  _6_bit_XOR_Gate u_6_bit_xor_1 (.A(in_1), .B(in_2), .O(out_3));

  // Notes on the sheet:
  //   A[5:0]
  //   B[5:0]
  //   O[5:0]
endmodule

module _6_bit_NOT_Gate (
  input  [5:0] in_1,
  output [5:0] out_2
);

  not not_1 (out_2[0], in_1[0]);
  not not_2 (out_2[1], in_1[1]);
  not not_3 (out_2[2], in_1[2]);
  not not_4 (out_2[3], in_1[3]);
  not not_5 (out_2[4], in_1[4]);
  not not_6 (out_2[5], in_1[5]);

  // Other names for the same wires on the sheet: A5 = in_1[0]; A4 = in_1[1]; A3 = in_1[2]; A2 = in_1[3]; A1 = in_1[4];
  //   A0 = in_1[5]; O5 = out_2[0]; O4 = out_2[1]; O3 = out_2[2]; O2 = out_2[3]; O1 = out_2[4]; O0 = out_2[5]
endmodule

module _6bit_NOT_Gate_Testing (
  input  [5:0] in_1,
  output [5:0] out_2
);

  _6_bit_NOT_Gate u_6_bit_not_1 (.in_1(in_1), .out_2(out_2));

  // Notes on the sheet:
  //   A[5:0]
  //   O[5:0]
endmodule

module ALU (
  input  [5:0] in_1,
  input  [5:0] in_2,
  input  OP,
  output [5:0] out_4,
  output SF,
  output ZF,
  output CF
);

  wire or_1_out;
  wire [5:0] NOT, XOR;

  _6_bit_XOR_Gate u_6_bit_xor_1 (.A(in_1), .B(in_2), .O(XOR));
  _6_bit_NOT_Gate u_6_bit_not_1 (.in_1(in_1), .out_2(NOT));
  Multiplexer #(.width(6), .enable("false")) multiplexer_1 (.in0(XOR), .in1(NOT), .out(out_4), .sel(OP));
  or or_1 (or_1_out, out_4[0], out_4[1], out_4[2], out_4[3], out_4[4], out_4[5]);
  not not_1 (ZF, or_1_out);

  assign CF = 1'b0;
  assign SF = out_4[5];

  // Other names for the same wires on the sheet: A[5:0] = in_1; B[5:0] = in_2

  // Notes on the sheet:
  //   A[5:0]
  //   B[5:0]
  //   R[5:0
endmodule

module ALU_Testing (
  input  [5:0] A_5_0,
  input  [5:0] B_5_0,
  input  OP,
  output [5:0] out_4,
  output CF,
  output SF,
  output ZF
);

  ALU alu_1 (.in_1(A_5_0), .in_2(B_5_0), .OP(OP), .out_4(out_4), .SF(SF), .CF(CF), .ZF(ZF));

  // Notes on the sheet:
  //   R[5:0]
endmodule

module _1_bit_Register (
  input  Din,
  input  Sel,
  input  Clock,
  output Dout
);

  wire multiplexer_1_out;

  Multiplexer #(.enable("false")) multiplexer_1 (.in0(Dout), .in1(Din), .out(multiplexer_1_out), .sel(Sel));
  D_Flip_Flop d_ff_1 (.clk(Clock), .D(multiplexer_1_out), .Q(Dout));  // open: Qn, preset, en, reset
endmodule

module _1_bit_2_to_1_MUX (
  input  A,
  input  Sel,
  input  B,
  output Out
);

  wire and_1_out, and_2_out, not_1_out;

  not not_1 (not_1_out, Sel);
  and and_1 (and_1_out, A, not_1_out);
  and and_2 (and_2_out, Sel, B);
  or or_1 (Out, and_1_out, and_2_out);
endmodule

module _6_bit_Register (
  input  [5:0] Din_5_0,
  input  Sel,
  input  Clock,
  output [5:0] Dout_5_0
);

  _1_bit_Register u_1_bit_register_1 (.Din(Din_5_0[5]), .Sel(Sel), .Clock(Clock), .Dout(Dout_5_0[5]));
  _1_bit_Register u_1_bit_register_2 (.Din(Din_5_0[4]), .Sel(Sel), .Clock(Clock), .Dout(Dout_5_0[4]));
  _1_bit_Register u_1_bit_register_3 (.Din(Din_5_0[3]), .Sel(Sel), .Clock(Clock), .Dout(Dout_5_0[3]));
  _1_bit_Register u_1_bit_register_4 (.Din(Din_5_0[2]), .Sel(Sel), .Clock(Clock), .Dout(Dout_5_0[2]));
  _1_bit_Register u_1_bit_register_5 (.Din(Din_5_0[1]), .Sel(Sel), .Clock(Clock), .Dout(Dout_5_0[1]));
  _1_bit_Register u_1_bit_register_6 (.Din(Din_5_0[0]), .Sel(Sel), .Clock(Clock), .Dout(Dout_5_0[0]));
endmodule

module Register_Set_with_3_6_bit_Register (
  input  REG_EN,
  input  [1:0] Wr_1_0,
  input  [5:0] in_3,
  input  Clock,
  input  [1:0] Rb_1_0,
  input  [1:0] Ra_1_0,
  output [5:0] out_7,
  output [5:0] out_8
);

  wire Reg0, Reg1, Reg2;
  wire [5:0] R0, R1, R2;

  Decoder #(.select(2)) decoder_1 (.out0(Reg0), .out1(Reg1), .out2(Reg2), .sel(Wr_1_0), .en(REG_EN));  // open: out3
  _6_bit_Register u_6_bit_register_1 (.Din_5_0(in_3), .Clock(Clock), .Dout_5_0(R0), .Sel(Reg0));
  _6_bit_Register u_6_bit_register_2 (.Din_5_0(in_3), .Clock(Clock), .Dout_5_0(R1), .Sel(Reg1));
  _6_bit_Register u_6_bit_register_3 (.Din_5_0(in_3), .Clock(Clock), .Dout_5_0(R2), .Sel(Reg2));
  Multiplexer #(.select(2), .width(6), .enable("false")) multiplexer_1 (
    .in0(R0), .in1(R1), .in2(R2), .out(out_7), .sel(Ra_1_0));  // open: in3
  Multiplexer #(.select(2), .width(6), .enable("false")) multiplexer_2 (
    .in0(R0), .in1(R1), .in2(R2), .out(out_8), .sel(Rb_1_0));  // open: in3

  // Notes on the sheet:
  //   6 bit 2 to 4 Decoder
  //   Wrd[5:0]
  //   6 bit 4 to 1MUX
  //   6 bit 4 to 1 MUX 
  //   A[5:0]
  //   B[5:0]
endmodule

module Flag_Register (
  input  CF,
  input  SF,
  input  ZF,
  input  Clock,
  output CF_2,
  output SF_2,
  output ZF_2
);

  _1_bit_Register u_1_bit_register_1 (.Din(CF), .Sel(1'b1), .Clock(Clock), .Dout(CF_2));
  _1_bit_Register u_1_bit_register_2 (.Din(SF), .Sel(1'b1), .Clock(Clock), .Dout(SF_2));
  _1_bit_Register u_1_bit_register_3 (.Din(ZF), .Sel(1'b1), .Clock(Clock), .Dout(ZF_2));
endmodule

module Register_Set_Testing (
  input  [1:0] Ra_1_0,
  input  [1:0] Rb_1_0,
  input  [1:0] Wr_1_0,
  input  REG_EN,
  input  [5:0] Wrd_5_0,
  input  in_6,
  output [5:0] A_5_0,
  output [5:0] B_5_0
);

  Register_Set_with_3_6_bit_Register register_set_with_3_6_bit_register_1 (
    .REG_EN(REG_EN), .Wr_1_0(Wr_1_0), .in_3(Wrd_5_0), .Clock(in_6), .Rb_1_0(Rb_1_0), .Ra_1_0(Ra_1_0),
    .out_7(A_5_0), .out_8(B_5_0));
endmodule

module _1x1_static_RAM_Cell (
  input  Read_Select_1,
  input  Read_Select_2,
  input  Write_Data,
  input  Write_Select,
  input  Clock,
  output Read_Data_1,
  output Read_Data_2
);

  wire d_ff_1_q, multiplexer_1_out;

  Multiplexer #(.enable("false")) multiplexer_1 (
    .in0(d_ff_1_q), .in1(Write_Data), .out(multiplexer_1_out), .sel(Write_Select));
  D_Flip_Flop d_ff_1 (.clk(Clock), .D(multiplexer_1_out), .Q(d_ff_1_q));  // open: Qn, preset, en, reset
  and and_1 (Read_Data_1, Read_Select_1, d_ff_1_q);
  and and_2 (Read_Data_2, Read_Select_2, d_ff_1_q);
endmodule

module _1x3_SRAM (
  input  Read_Select_1,
  input  Read_Select_2,
  input  Write_Select,
  input  [2:0] Write_Data,
  input  Clock,
  output [2:0] Read_Data_1,
  output [2:0] Read_Date_2
);

  _1x1_static_RAM_Cell u_1x1_static_ram_cell_1 (
    .Write_Data(Write_Data[0]), .Write_Select(Write_Select), .Clock(Clock), .Read_Data_1(Read_Data_1[0]),
    .Read_Data_2(Read_Date_2[0]), .Read_Select_1(Read_Select_1), .Read_Select_2(Read_Select_2));
  _1x1_static_RAM_Cell u_1x1_static_ram_cell_2 (
    .Write_Data(Write_Data[1]), .Write_Select(Write_Select), .Clock(Clock), .Read_Data_1(Read_Data_1[1]),
    .Read_Data_2(Read_Date_2[1]), .Read_Select_1(Read_Select_1), .Read_Select_2(Read_Select_2));
  _1x1_static_RAM_Cell u_1x1_static_ram_cell_3 (
    .Write_Data(Write_Data[2]), .Write_Select(Write_Select), .Clock(Clock), .Read_Data_1(Read_Data_1[2]),
    .Read_Data_2(Read_Date_2[2]), .Read_Select_1(Read_Select_1), .Read_Select_2(Read_Select_2));
endmodule

module _1x18_SRAM (
  input  Read_Select_2,
  input  Read_Select_1,
  input  Write_Select,
  input  [17:0] WriteData_17_0,
  input  Clock,
  output [17:0] Read_Data_1_17_0,
  output [17:0] Read_Data_2_17_0
);

  _1x3_SRAM u_1x3_sram_1 (
    .Read_Select_1(Read_Select_2), .Read_Select_2(Read_Select_1), .Write_Select(Write_Select),
    .Write_Data(WriteData_17_0[2:0]), .Clock(Clock), .Read_Data_1(Read_Data_1_17_0[2:0]),
    .Read_Date_2(Read_Data_2_17_0[2:0]));
  _1x3_SRAM u_1x3_sram_2 (
    .Read_Select_1(Read_Select_2), .Read_Select_2(Read_Select_1), .Write_Select(Write_Select),
    .Write_Data(WriteData_17_0[5:3]), .Clock(Clock), .Read_Data_1(Read_Data_1_17_0[5:3]),
    .Read_Date_2(Read_Data_2_17_0[5:3]));
  _1x3_SRAM u_1x3_sram_3 (
    .Read_Select_1(Read_Select_2), .Read_Select_2(Read_Select_1), .Write_Select(Write_Select),
    .Write_Data(WriteData_17_0[8:6]), .Clock(Clock), .Read_Data_1(Read_Data_1_17_0[8:6]),
    .Read_Date_2(Read_Data_2_17_0[8:6]));
  _1x3_SRAM u_1x3_sram_4 (
    .Read_Select_1(Read_Select_2), .Read_Select_2(Read_Select_1), .Write_Select(Write_Select),
    .Write_Data(WriteData_17_0[11:9]), .Clock(Clock), .Read_Data_1(Read_Data_1_17_0[11:9]),
    .Read_Date_2(Read_Data_2_17_0[11:9]));
  _1x3_SRAM u_1x3_sram_5 (
    .Read_Select_1(Read_Select_2), .Read_Select_2(Read_Select_1), .Write_Select(Write_Select),
    .Write_Data(WriteData_17_0[14:12]), .Clock(Clock), .Read_Data_1(Read_Data_1_17_0[14:12]),
    .Read_Date_2(Read_Data_2_17_0[14:12]));
  _1x3_SRAM u_1x3_sram_6 (
    .Read_Select_1(Read_Select_2), .Read_Select_2(Read_Select_1), .Write_Select(Write_Select),
    .Write_Data(WriteData_17_0[17:15]), .Clock(Clock), .Read_Data_1(Read_Data_1_17_0[17:15]),
    .Read_Date_2(Read_Data_2_17_0[17:15]));
endmodule

module _7x18_SRAM (
  input  [17:0] Write_Data_17_0,
  input  Write_Enable,
  input  [2:0] Write_Address__2_0,
  input  [2:0] Read_Address_1_2_0,
  input  [2:0] Read_Address_2_2_0,
  input  Clock,
  output [17:0] Read_Data1_17_0,
  output [17:0] Read_Data2_17_0
);

  wire R1_0, R1_1, R1_2, R1_3, R1_4, R1_5, R1_6, R2_0, R2_1, R2_2, R2_3, R2_4, R2_5, R2_6, W0, W1, W2, W3,
       W4, W5, W6;
  wire [17:0] RD1_0, RD1_1, RD1_2, RD1_3, RD1_4, RD1_5, RD2_0, RD2_1, RD2_2, RD2_3, Rd2_3_t, RD2_4, RD2_5,
       RD2_6;

  Decoder #(.select(3)) decoder_1 (
    .out0(W0), .out1(W1), .out2(W2), .out3(W3), .out4(W4), .out5(W5), .out6(W6), .sel(Write_Address__2_0),
    .en(Write_Enable));  // open: out7
  Decoder #(.select(3), .enable("false")) decoder_2 (
    .out0(R1_0), .out1(R1_1), .out2(R1_2), .out3(R1_3), .out4(R1_4), .out5(R1_5), .out6(R1_6),
    .sel(Read_Address_1_2_0));  // open: out7
  Decoder #(.select(3), .enable("false")) decoder_3 (
    .out0(R2_0), .out1(R2_1), .out2(R2_2), .out3(R2_3), .out4(R2_4), .out5(R2_5), .out6(R2_6),
    .sel(Read_Address_2_2_0));  // open: out7
  _1x18_SRAM u_1x18_sram_1 (
    .Read_Select_2(R1_0), .Read_Select_1(R2_0), .Write_Select(W0), .WriteData_17_0(Write_Data_17_0),
    .Clock(Clock), .Read_Data_1_17_0(RD1_0), .Read_Data_2_17_0(RD2_0));
  _1x18_SRAM u_1x18_sram_2 (
    .Read_Select_2(R1_1), .Read_Select_1(R2_1), .Write_Select(W1), .WriteData_17_0(Write_Data_17_0),
    .Clock(Clock), .Read_Data_1_17_0(RD1_1), .Read_Data_2_17_0(RD2_1));
  _1x18_SRAM u_1x18_sram_3 (
    .Read_Select_2(R1_2), .Read_Select_1(R2_2), .Write_Select(W2), .WriteData_17_0(Write_Data_17_0),
    .Clock(Clock), .Read_Data_1_17_0(RD1_2), .Read_Data_2_17_0(RD2_2));
  _1x18_SRAM u_1x18_sram_4 (
    .Read_Select_2(R1_3), .Read_Select_1(R2_3), .Write_Select(W3), .WriteData_17_0(Write_Data_17_0),
    .Clock(Clock), .Read_Data_1_17_0(RD1_3), .Read_Data_2_17_0(Rd2_3_t));
  _1x18_SRAM u_1x18_sram_5 (
    .Read_Select_2(R1_4), .Read_Select_1(R2_4), .Write_Select(W4), .WriteData_17_0(Write_Data_17_0),
    .Clock(Clock), .Read_Data_1_17_0(RD1_4), .Read_Data_2_17_0(RD2_4));
  _1x18_SRAM u_1x18_sram_6 (
    .Read_Select_2(R1_5), .Read_Select_1(R2_5), .Write_Select(W5), .WriteData_17_0(Write_Data_17_0),
    .Clock(Clock), .Read_Data_1_17_0(RD1_5), .Read_Data_2_17_0(RD2_5));
  assign Read_Data1_17_0 = RD1_0 | RD1_1 | RD1_2 | RD1_3 | RD1_4 | RD1_5 | RD1_5;  // OR_Gate or_1, 18 bits wide
  assign Read_Data2_17_0 = RD2_0 | RD2_1 | RD2_2 | RD2_3 | RD2_4 | RD2_5 | RD2_6;  // OR_Gate or_2, 18 bits wide
endmodule

module RAM_Testing (
  input  [2:0] Read_Address_2_0,
  input  [2:0] Read_Address_2_0_2,
  input  [2:0] Write_Address_2_0,
  input  [17:0] Write_Data_17_0,
  input  Write_Enable,
  input  Clock,
  output [17:0] Read_Data_1_17_0,
  output [17:0] Read_Data_2_17_0
);

  _7x18_SRAM u_7x18_sram_1 (
    .Write_Data_17_0(Write_Data_17_0), .Write_Enable(Write_Enable), .Write_Address__2_0(Write_Address_2_0),
    .Read_Address_1_2_0(Read_Address_2_0), .Read_Address_2_2_0(Read_Address_2_0_2), .Clock(Clock),
    .Read_Data1_17_0(Read_Data_1_17_0), .Read_Data2_17_0(Read_Data_2_17_0));
endmodule

module _3_bit_Program_Counter (
  input  [2:0] I_2_0,
  input  Clock,
  output [2:0] O_2_0
);

  D_Flip_Flop d_ff_1 (.clk(Clock), .D(I_2_0[2]), .Q(O_2_0[2]));  // open: Qn, preset, en, reset
  D_Flip_Flop d_ff_2 (.clk(Clock), .D(I_2_0[1]), .Q(O_2_0[1]));  // open: Qn, preset, en, reset
  D_Flip_Flop d_ff_3 (.clk(Clock), .D(I_2_0[0]), .Q(O_2_0[0]));  // open: Qn, preset, en, reset
endmodule

module _3_bit_PC_Adder (
  input  [2:0] Input_Address_2_0,
  output [2:0] Output_Address_2_0
);

  wire [2:0] bit_extender_1_out;

  assign bit_extender_1_out = {{2{1'b0}}, 1'b1};  // Bit_Extender bit_extender_1
  Adder #(.width(3)) adder_1 (
    .a(Input_Address_2_0), .b(bit_extender_1_out), .out(Output_Address_2_0), .cin(1'b0));  // open: cout
endmodule

module ROM (
  input  Clock,
  input  PC_Enable,
  output [2:0] Physical_Address,
  output [17:0] Data,
  output Write_Enable,
  output PC_Clock
);

  wire [19:18] rom_1_data;

  Counter #(.width(3), .max('h7)) counter_1 (.Q(Physical_Address), .clk(Clock));  // open: load, D, count, carry, clr
  not not_1 (Write_Enable, PC_Enable);
  and and_1 (PC_Clock, Clock, PC_Enable);
  ROM_part #(.addrWidth(3), .dataWidth(20)) rom_1 (.addr(Physical_Address), .data({rom_1_data, Data}));  // open: sel

  // Notes on the sheet:
  //   contents of rom_1 (hex, n*v repeats v):
  //   3000 8000 12380 1c000 24000 800 10380 23000
endmodule

module Control_Unit (
  input  [2:0] Opcode_2_0,
  input  ZF,
  input  SF,
  input  CF,
  output Imm_Sel,
  output REG_EN,
  output OP,
  output Jmp_Sel
);

  wire and_1_out, Imm_2_out, JLE_out, Jmp_2_out, Jmp_out, not_1_out, not_2_out, not_3_out, not_4_out,
       not_5_out, not_6_out, not_7_out, or_1_out, or_2_out, Reg_out;

  not not_1 (not_1_out, Opcode_2_0[2]);
  not not_2 (not_2_out, Opcode_2_0[1]);
  not not_3 (not_3_out, Opcode_2_0[2]);
  not not_4 (not_4_out, Opcode_2_0[2]);
  not not_5 (not_5_out, Opcode_2_0[1]);
  not not_6 (not_6_out, Opcode_2_0[1]);
  and Imm (Imm_Sel, not_1_out, Opcode_2_0[1]);
  and Jmp (Jmp_out, Opcode_2_0[2], not_2_out);
  and Imm_2 (Imm_2_out, not_3_out, Opcode_2_0[1]);
  and Reg (Reg_out, not_4_out, not_5_out);
  and Jmp_2 (Jmp_2_out, Opcode_2_0[2], not_6_out);
  and and_1 (and_1_out, Imm_2_out, Reg_out);
  or or_1 (or_1_out, SF, ZF);
  or or_2 (or_2_out, Jmp_out, and_1_out);
  not not_7 (not_7_out, Opcode_2_0[0]);
  and JLE (JLE_out, or_1_out, not_7_out);
  not not_8 (REG_EN, or_2_out);
  and and_2 (Jmp_Sel, JLE_out, Jmp_2_out);

  assign OP = Opcode_2_0[0];
endmodule

module _6_bit_CPU (
  input  PC_Enable
);

  wire alu_1_cf, alu_1_sf, alu_1_zf, CF, CLK, CPU_CLK, Imm_Sel, Jmp_Sel, OP, REG_EN, ROM_WE, SF, ZF;
  wire [1:0] n7x18_sram_1_read_data1_17_0_2;
  wire [2:0] multiplexer_1_out, n3_bit_pc_adder_1_output_address_2_0, n3_bit_program_counter_1_o_2_0,
       Phy_Address;
  wire [2:1] n7x18_sram_1_read_data1_17_0_3;
  wire [5:0] alu_1_out_4, multiplexer_2_out, register_set_with_3_6_bit_register_1_out_7,
       register_set_with_3_6_bit_register_1_out_8;
  wire [17:0] n7x18_sram_1_read_data1_17_0, ROM_Data;

  Clock Clock (.out(CLK));
  Multiplexer #(.width(3), .enable("false")) multiplexer_1 (
    .in0(n3_bit_pc_adder_1_output_address_2_0),
    .in1({n7x18_sram_1_read_data1_17_0_3, n7x18_sram_1_read_data1_17_0_2[1]}), .out(multiplexer_1_out),
    .sel(Jmp_Sel));
  _3_bit_PC_Adder u_3_bit_pc_adder_1 (
    .Input_Address_2_0(n3_bit_program_counter_1_o_2_0),
    .Output_Address_2_0(n3_bit_pc_adder_1_output_address_2_0));
  _3_bit_Program_Counter u_3_bit_program_counter_1 (
    .I_2_0(multiplexer_1_out), .Clock(CPU_CLK), .O_2_0(n3_bit_program_counter_1_o_2_0));
  ROM rom_1 (
    .Clock(CLK), .PC_Enable(PC_Enable), .Physical_Address(Phy_Address), .Data(ROM_Data),
    .Write_Enable(ROM_WE), .PC_Clock(CPU_CLK));
  _7x18_SRAM u_7x18_sram_1 (
    .Write_Data_17_0(ROM_Data), .Write_Enable(ROM_WE), .Write_Address__2_0(Phy_Address),
    .Read_Address_1_2_0(n3_bit_program_counter_1_o_2_0), .Clock(CLK),
    .Read_Data1_17_0({n7x18_sram_1_read_data1_17_0[17:15], n7x18_sram_1_read_data1_17_0_3, n7x18_sram_1_read_data1_17_0_2, n7x18_sram_1_read_data1_17_0[10:0]}));  // open: Read_Address_2_2_0, Read_Data2_17_0
  Control_Unit control_unit_1 (
    .Opcode_2_0(n7x18_sram_1_read_data1_17_0[17:15]), .ZF(ZF), .SF(SF), .CF(CF), .Imm_Sel(Imm_Sel),
    .REG_EN(REG_EN), .OP(OP), .Jmp_Sel(Jmp_Sel));
  Register_Set_with_3_6_bit_Register register_set_with_3_6_bit_register_1 (
    .REG_EN(REG_EN), .Wr_1_0(n7x18_sram_1_read_data1_17_0_3), .in_3(alu_1_out_4), .Clock(CPU_CLK),
    .Rb_1_0(n7x18_sram_1_read_data1_17_0_2), .Ra_1_0(n7x18_sram_1_read_data1_17_0_3),
    .out_7(register_set_with_3_6_bit_register_1_out_7), .out_8(register_set_with_3_6_bit_register_1_out_8));
  Flag_Register flag_register_1 (
    .CF(alu_1_cf), .SF(alu_1_sf), .ZF(alu_1_zf), .Clock(CPU_CLK), .CF_2(CF), .SF_2(SF), .ZF_2(ZF));
  Multiplexer #(.width(6), .enable("false")) multiplexer_2 (
    .in0(register_set_with_3_6_bit_register_1_out_8),
    .in1({n7x18_sram_1_read_data1_17_0_2, n7x18_sram_1_read_data1_17_0[10:7]}), .out(multiplexer_2_out),
    .sel(Imm_Sel));
  ALU alu_1 (
    .in_1(register_set_with_3_6_bit_register_1_out_7), .in_2(multiplexer_2_out), .OP(OP),
    .out_4(alu_1_out_4), .SF(alu_1_sf), .CF(alu_1_cf), .ZF(alu_1_zf));

  // Notes on the sheet:
  //   Register Mode XOR = 00 0 01 10 00000000000
  //   Immediate Mode XOR = 01 0 01 000111 0000000
  //   Branching Mode JLE = 10 0 100 000000000000
  //   Branching Mode: Opcode(2bit+1bit)+Address(3 bit)+Unused(12 bit) --> Opcode 1st 2 bit =00 + Opcode last 1 bit = JLE(0)
  //   Register Mode: Opcode(2bit+1bit)+Register RA(2 bit)+Register RB(2 bit)+Unused(11 bit) --> Opcode 1st 2 bit =00 + Opcode last 1 bit = XOR(0) , NOT(1)
  //   Immediate Mode: Opcode(2bit+1bit)+Register RA(2 bit)+Immediate Value (6 bit)+Unused(7 bit) --> Opcode 1st 2 bit =00 + Opcode last 1 bit = XOR(0) , NOT(1)
  //   Register Mode NOT= 00 1 00 0000000000000
  //   Immediate Mode NOT= 01 1 10 000000 0000000
endmodule
